// Logisim project 2bit_2s_complement.circ as structural Verilog: 1 circuit, main circuit main
module main (
  input  a,
  input  b,
  output x,
  output y
);

  wire not_1_out, not_2_out;

  not not_1 (not_1_out, a);
  not not_2 (not_2_out, b);
  xor xor_1 (x, not_1_out, not_2_out);

  assign y = b;
endmodule
