// Logisim project 3bit_2s_complement.circ as structural Verilog: 1 circuit, main circuit main
module main (
  input  in_1,
  input  in_2,
  input  in_3,
  output out_4,
  output out_5,
  output out_6
);

  wire and_1_out, not_1_out, not_2_out, not_3_out;

  not not_1 (not_1_out, in_1);
  not not_2 (not_2_out, in_2);
  not not_3 (not_3_out, in_3);
  and and_1 (and_1_out, not_2_out, not_3_out);
  xor xor_1 (out_4, not_1_out, and_1_out);
  xor xor_2 (out_5, not_2_out, not_3_out);

  assign out_6 = in_3;
endmodule
