// Logisim project a02.circ as structural Verilog: 8 circuits, main circuit main
module main (
  input  in_1,
  input  in_2,
  input  in_3,
  input  in_4,
  input  in_5,
  input  in_6,
  input  in_7,
  input  in_8,
  input  in_9,
  output out_10,
  output out_11,
  output out_12,
  output out_13
);

  my_adder my_adder_1 (
    .a0(in_1), .a1(in_2), .a2(in_3), .a3(in_4), .b0(in_5), .b1(in_6), .b2(in_7), .b3(in_8), .s(in_9),
    .out_10(out_10), .out_11(out_11), .out_12(out_12), .out_13(out_13));
endmodule

module my_1_half_adder (
  input  a1,
  input  a2,
  output s,
  output c
);

  xor xor_1 (s, a1, a2);
  and and_1 (c, a1, a2);
endmodule

module my_full_adder (
  input  x,
  input  y,
  input  z,
  output s,
  output c
);

  wire my_1_half_adder_1_c, my_1_half_adder_1_s, my_1_half_adder_2_c;

  my_1_half_adder my_1_half_adder_1 (.a1(x), .a2(y), .s(my_1_half_adder_1_s), .c(my_1_half_adder_1_c));
  my_1_half_adder my_1_half_adder_2 (.a1(my_1_half_adder_1_s), .a2(z), .s(s), .c(my_1_half_adder_2_c));
  or or_1 (c, my_1_half_adder_2_c, my_1_half_adder_1_c);
endmodule

module four_bit_adder (
  input  a0,
  input  a1,
  input  a2,
  input  a3,
  input  b0,
  input  b1,
  input  b2,
  input  b3,
  output c0,
  output c1,
  output c2,
  output c3,
  output c
);

  wire my_full_adder_1_c, my_full_adder_2_c, my_full_adder_3_c;

  my_full_adder my_full_adder_1 (.x(1'b0), .y(a0), .z(b0), .s(c0), .c(my_full_adder_1_c));
  my_full_adder my_full_adder_2 (.x(my_full_adder_1_c), .y(a1), .z(b1), .s(c1), .c(my_full_adder_2_c));
  my_full_adder my_full_adder_3 (.x(my_full_adder_2_c), .y(a2), .z(b2), .s(c2), .c(my_full_adder_3_c));
  my_full_adder my_full_adder_4 (.x(my_full_adder_3_c), .y(a3), .z(b3), .s(c3), .c(c));
endmodule

module my_multiplexer (
  input  a,
  input  b,
  input  in_3,
  output out_4
);

  wire and_1_out, and_2_out, not_1_out, or_1_out;

  or or_1 (or_1_out, a, in_3);
  not not_1 (not_1_out, in_3);
  and and_1 (and_1_out, or_1_out, b);
  and and_2 (and_2_out, a, not_1_out);
  or or_2 (out_4, and_1_out, and_2_out);
endmodule

module four_bit_multiplexor (
  input  a0,
  input  a1,
  input  a2,
  input  a3,
  input  b0,
  input  b1,
  input  b2,
  input  b3,
  input  s,
  output c0,
  output c1,
  output c2,
  output c3
);

  my_multiplexer my_multiplexer_1 (.a(a0), .b(b0), .in_3(s), .out_4(c0));
  my_multiplexer my_multiplexer_2 (.a(a1), .b(b1), .in_3(s), .out_4(c1));
  my_multiplexer my_multiplexer_3 (.a(a2), .b(b2), .in_3(s), .out_4(c2));
  my_multiplexer my_multiplexer_4 (.a(a3), .b(b3), .in_3(s), .out_4(c3));
endmodule

module four_bit_2_complement (
  input  a,
  input  b,
  input  c,
  input  d,
  output a1,
  output b1,
  output c1,
  output d1
);

  wire and_1_out, and_2_out, and_3_out, and_4_out, and_5_out, and_6_out, and_7_out, and_8_out, and_9_out,
       not_1_out, not_2_out, not_3_out, not_4_out;

  not not_1 (not_1_out, a);
  not not_2 (not_2_out, b);
  not not_3 (not_3_out, c);
  not not_4 (not_4_out, d);
  and and_1 (and_1_out, not_1_out, d);
  and and_2 (and_2_out, not_1_out, c);
  and and_3 (and_3_out, not_1_out, b);
  and and_4 (and_4_out, a, not_2_out, not_3_out, not_4_out);
  and and_5 (and_5_out, not_2_out, d);
  and and_6 (and_6_out, not_2_out, c);
  and and_7 (and_7_out, b, not_3_out, not_4_out);
  and and_8 (and_8_out, not_3_out, d);
  and and_9 (and_9_out, c, not_4_out);
  or or_1 (a1, and_1_out, and_2_out, and_3_out, and_4_out);
  or or_2 (b1, and_5_out, and_6_out, and_7_out);
  or or_3 (c1, and_8_out, and_9_out);

  assign d1 = d;
endmodule

module my_adder (
  input  a0,
  input  a1,
  input  a2,
  input  a3,
  input  b0,
  input  b1,
  input  b2,
  input  b3,
  input  s,
  output out_10,
  output out_11,
  output out_12,
  output out_13
);

  wire four_bit_2_complement_1_a1, four_bit_2_complement_1_b1, four_bit_2_complement_1_c1,
       four_bit_2_complement_1_d1, four_bit_adder_1_c, four_bit_multiplexor_1_c0, four_bit_multiplexor_1_c1,
       four_bit_multiplexor_1_c2, four_bit_multiplexor_1_c3;

  four_bit_2_complement four_bit_2_complement_1 (
    .a(b3), .b(b2), .c(b1), .d(b0), .a1(four_bit_2_complement_1_a1), .b1(four_bit_2_complement_1_b1),
    .c1(four_bit_2_complement_1_c1), .d1(four_bit_2_complement_1_d1));
  four_bit_multiplexor four_bit_multiplexor_1 (
    .a0(b0), .a1(b1), .a2(b2), .a3(b3), .b0(four_bit_2_complement_1_d1), .b1(four_bit_2_complement_1_c1),
    .b2(four_bit_2_complement_1_b1), .b3(four_bit_2_complement_1_a1), .s(s), .c0(four_bit_multiplexor_1_c0),
    .c1(four_bit_multiplexor_1_c1), .c2(four_bit_multiplexor_1_c2), .c3(four_bit_multiplexor_1_c3));
  four_bit_adder four_bit_adder_1 (
    .a0(a0), .a1(a1), .a2(a2), .a3(a3), .b0(four_bit_multiplexor_1_c0), .b1(four_bit_multiplexor_1_c1),
    .b2(four_bit_multiplexor_1_c2), .b3(four_bit_multiplexor_1_c3), .c0(out_10), .c1(out_11), .c2(out_12),
    .c3(out_13), .c(four_bit_adder_1_c));
  // also tied to GND on the sheet: four_bit_adder_1_c
endmodule
