// Logisim project Assignment3.circ as structural Verilog: 10 circuits, main circuit main
module main (
  input  in_1,
  input  in_2,
  input  in_3,
  input  in_4
);

  wire fifth_light_1_x, first_light_1_x, fourth_light_1_x, second_light_1_out_5, sixth_light_1_x,
       third_light_1_x, zero_light_1_out_5;

  sixth_light sixth_light_1 (.a(in_1), .b(in_2), .c(in_3), .d(in_4), .x(sixth_light_1_x));
  fifth_light fifth_light_1 (.a(in_1), .b(in_2), .c(in_3), .d(in_4), .x(fifth_light_1_x));
  fourth_light fourth_light_1 (.a(in_1), .b(in_2), .c(in_3), .d(in_4), .x(fourth_light_1_x));
  zero_light zero_light_1 (.a(in_1), .b(in_2), .c(in_3), .d(in_4), .out_5(zero_light_1_out_5));
  first_light first_light_1 (.a(in_1), .b(in_2), .c(in_3), .d(in_4), .x(first_light_1_x));
  second_light second_light_1 (.a1(in_1), .b1(in_2), .c1(in_3), .d1(in_4), .out_5(second_light_1_out_5));
  third_light third_light_1 (.a(in_1), .b(in_2), .c(in_3), .d(in_4), .x(third_light_1_x));
  _7_Segment_Display u_7_segment_display_1 (
    .g(sixth_light_1_x), .f(fifth_light_1_x), .a(zero_light_1_out_5), .b(first_light_1_x),
    .e(fourth_light_1_x), .d(third_light_1_x), .c(second_light_1_out_5));  // open: dp
endmodule

module second_light (
  input  a1,
  input  b1,
  input  c1,
  input  d1,
  output out_5
);

  wire and_1_out, and_2_out, and_3_out, not_1_out, not_2_out, not_3_out, or_1_out, or_2_out, or_3_out;

  not not_1 (not_1_out, a1);
  not not_2 (not_2_out, b1);
  not not_3 (not_3_out, c1);
  // NOT_Gate not_4 has open pins: in=d1, out=open
  and and_1 (and_1_out, not_1_out, b1);
  and and_2 (and_2_out, not_3_out, d1);
  or or_1 (or_1_out, a1, not_3_out);
  or or_2 (or_2_out, or_1_out, d1);
  and and_3 (and_3_out, not_2_out, or_2_out);
  or or_3 (or_3_out, and_1_out, and_3_out);
  or or_4 (out_5, or_3_out, and_2_out);
endmodule

module zero_light (
  input  a,
  input  b,
  input  c,
  input  d,
  output out_5
);

  wire and_1_out, and_2_out, not_1_out, not_2_out, not_3_out, not_4_out, not_5_out, or_1_out, or_2_out,
       or_3_out, or_4_out, or_5_out, or_6_out, or_7_out;

  not not_1 (not_1_out, a);
  not not_2 (not_2_out, b);
  not not_3 (not_3_out, d);
  or or_1 (or_1_out, not_1_out, b);
  or or_2 (or_2_out, a, not_2_out);
  and and_1 (and_1_out, or_2_out, not_3_out);
  or or_3 (or_3_out, or_1_out, not_3_out);
  or or_4 (or_4_out, or_1_out, c);
  or or_5 (or_5_out, or_2_out, not_3_out);
  and and_2 (and_2_out, or_3_out, c);
  not not_4 (not_4_out, or_4_out);
  not not_5 (not_5_out, or_5_out);
  or or_6 (or_6_out, and_1_out, and_2_out);
  or or_7 (or_7_out, not_4_out, not_5_out);
  or or_8 (out_5, or_6_out, or_7_out);
endmodule

module first_light (
  input  a,
  input  b,
  input  c,
  input  d,
  output x
);

  wire and_1_out, and_2_out, and_3_out, and_4_out, and_5_out, not_1_out, not_2_out, not_3_out, not_4_out;

  not not_1 (not_1_out, a);
  not not_2 (not_2_out, b);
  not not_3 (not_3_out, c);
  not not_4 (not_4_out, d);
  and and_1 (and_1_out, not_1_out, not_3_out, not_4_out);
  and and_2 (and_2_out, not_1_out, c, d);
  and and_3 (and_3_out, not_2_out, not_4_out);
  and and_4 (and_4_out, a, not_3_out, d);
  and and_5 (and_5_out, not_1_out, not_2_out);
  or or_1 (x, and_1_out, and_2_out, and_3_out, and_4_out, and_5_out);
endmodule

module third_light (
  input  a,
  input  b,
  input  c,
  input  d,
  output x
);

  wire and_1_out, and_2_out, and_3_out, and_4_out, and_5_out, not_1_out, not_2_out, not_3_out, not_4_out;

  not not_1 (not_1_out, a);
  not not_2 (not_2_out, b);
  not not_3 (not_3_out, c);
  not not_4 (not_4_out, d);
  and and_1 (and_1_out, b, not_3_out, d);
  and and_2 (and_2_out, not_2_out, c, d);
  and and_3 (and_3_out, not_1_out, not_2_out, not_4_out);
  and and_4 (and_4_out, a, not_3_out, not_4_out);
  and and_5 (and_5_out, b, c, not_4_out);
  or or_1 (x, and_1_out, and_2_out, and_3_out, and_4_out, and_5_out);
endmodule

module fourth_light (
  input  a,
  input  b,
  input  c,
  input  d,
  output x
);

  wire and_1_out, and_2_out, and_3_out, not_1_out, not_2_out, not_3_out, or_1_out, or_2_out;

  not not_1 (not_1_out, a);
  not not_2 (not_2_out, b);
  not not_3 (not_3_out, d);
  and and_1 (and_1_out, not_1_out, not_2_out);
  or or_1 (or_1_out, b, c, not_3_out);
  or or_2 (or_2_out, c, and_1_out);
  and and_2 (and_2_out, a, or_1_out);
  or or_3 (x, and_2_out, and_3_out);
  and and_3 (and_3_out, not_3_out, or_2_out);
endmodule

module fifth_light (
  input  a,
  input  b,
  input  c,
  input  d,
  output x
);

  wire and_1_out, and_2_out, and_3_out, and_4_out, and_5_out, not_1_out, not_2_out, not_3_out, not_4_out;

  not not_1 (not_1_out, a);
  not not_2 (not_2_out, b);
  not not_3 (not_3_out, c);
  not not_4 (not_4_out, d);
  and and_1 (and_1_out, not_3_out, not_4_out);
  and and_2 (and_2_out, not_1_out, b, not_3_out);
  and and_3 (and_3_out, b, not_4_out);
  and and_4 (and_4_out, a, not_2_out);
  and and_5 (and_5_out, a, c);
  or or_1 (x, and_1_out, and_2_out, and_3_out, and_4_out, and_5_out);
endmodule

module sixth_light (
  input  a,
  input  b,
  input  c,
  input  d,
  output x
);

  wire and_1_out, and_2_out, and_3_out, and_4_out, and_5_out, not_1_out, not_2_out, not_3_out, not_4_out;

  not not_1 (not_1_out, a);
  not not_2 (not_2_out, b);
  not not_3 (not_3_out, c);
  not not_4 (not_4_out, d);
  and and_1 (and_1_out, not_2_out, c);
  and and_2 (and_2_out, a, not_2_out);
  and and_3 (and_3_out, not_1_out, b, not_3_out);
  and and_4 (and_4_out, c, not_4_out);
  and and_5 (and_5_out, a, d);
  or or_1 (x, and_1_out, and_2_out, and_3_out, and_4_out, and_5_out);
endmodule

module seventh_light (
  input  a,
  input  b,
  input  c,
  input  d,
  output out_5
);
endmodule

module test (
  input  a1,
  input  b1,
  input  c1,
  input  d1,
  output out_5
);

  wire and_1_out, and_2_out, and_3_out, and_4_out, nor_1_out, not_1_out, not_2_out, not_3_out, or_1_out,
       xor_1_out;

  not not_1 (not_1_out, b1);
  not not_2 (not_2_out, d1);
  and and_1 (and_1_out, b1, c1);
  nor nor_1 (nor_1_out, a1, d1);
  and and_2 (and_2_out, not_1_out, c1);
  xor xor_1 (xor_1_out, c1, d1);
  not not_3 (not_3_out, and_1_out);
  and and_3 (and_3_out, not_3_out, nor_1_out);
  and and_4 (and_4_out, and_2_out, not_2_out);
  or or_1 (or_1_out, and_4_out, xor_1_out);
  or or_2 (out_5, and_3_out, or_1_out);
endmodule
